// Logisim project control.circ as structural Verilog: 1 circuit, main circuit main
module main (
  input  zb,
  input  button,
  input  cout,
  input  CLK,
  output diffE,
  output llE,
  output lrE,
  output clr,
  output CE,
  output diffS
);

  wire and_2_out, and_3_out, and_4_out, and_5_out, and_6_out, and_7_out, and_8_out, and_9_out, and_10_out,
       and_11_out, and_12_out, and_13_out, not_1_out, not_2_out, not_3_out, not_4_out, not_5_out, or_1_out,
       or_2_out, xor_1_out;
  wire [2:0] or_4_out, register_1_q;

  not not_1 (not_1_out, register_1_q[2]);
  Register #(.width(3)) register_1 (.D(or_4_out), .en(1'b1), .Q(register_1_q), .clk(CLK));  // open: clr
  and and_1 (or_4_out[2], zb, register_1_q[1], register_1_q[0], not_1_out);
  and and_2 (and_2_out, not_1_out, register_1_q[0]);
  and and_3 (and_3_out, register_1_q[1], not_4_out);
  and and_4 (and_4_out, not_1_out, not_2_out);
  not not_2 (not_2_out, cout);
  and and_5 (and_5_out, not_1_out, not_3_out);
  and and_6 (and_6_out, button, not_4_out);
  not not_3 (not_3_out, register_1_q[1]);
  not not_4 (not_4_out, register_1_q[0]);
  and and_7 (and_7_out, and_3_out, or_1_out);
  or or_1 (or_1_out, register_1_q[2], and_4_out);
  and and_8 (and_8_out, and_5_out, or_2_out);
  or or_2 (or_2_out, and_6_out, register_1_q[0]);
  and and_9 (and_9_out, not_1_out, register_1_q[1], not_4_out, not_5_out);
  not not_5 (not_5_out, cout);
  and and_10 (and_10_out, not_1_out, register_1_q[0]);
  and and_11 (and_11_out, register_1_q[2], register_1_q[1], not_4_out);
  and and_12 (and_12_out, register_1_q[1], not_4_out);
  and and_13 (and_13_out, not_1_out, not_3_out, register_1_q[0]);
  xor xor_1 (xor_1_out, register_1_q[1], register_1_q[0]);
  and and_14 (lrE, not_1_out, xor_1_out);
  and and_15 (clr, not_1_out, not_3_out, register_1_q[0]);
  and and_16 (CE, not_1_out, register_1_q[1], not_4_out);
  and and_17 (diffS, register_1_q[2], register_1_q[1], not_4_out);
  or or_3 (or_4_out[1], and_2_out, and_7_out);
  or or_4 (or_4_out[0], and_8_out, and_9_out);
  or or_5 (diffE, and_10_out, and_11_out);
  or or_6 (llE, and_12_out, and_13_out);

  // Notes on the sheet:
  //   N2
  //   N1
  //   N0
endmodule
