// Logisim project datapath.circ as structural Verilog: 5 circuits, main circuit main
module main (
  input  CE,
  input  [31:0] multiplier,
  input  clr,
  input  llE,
  input  lrE,
  input  [31:0] multiplicand,
  input  dffS,
  input  CLK,
  input  dffE,
  output shfOut,
  output overflow,
  output cout,
  output zeroBit,
  output [31:0] right,
  output [31:0] left
);

  wire fulladder32bit_1_carryout, multiplexer_1_out;
  wire [31:0] fulladder32bit_1_sum;

  Counter #(.width(5), .max('h1f)) counter_1 (.count(CE), .carry(cout), .clk(CLK), .clr(clr));  // open: load, D, Q
  shiftRegister64bit shiftregister64bit_1 (
    .shiftEn(CE), .leftRest(clr), .CLK(CLK), .llE(llE), .lrE(lrE), .leftIn(fulladder32bit_1_sum),
    .shiftInBit(overflow), .shiftOutBit(shfOut), .rightIn(multiplier), .leftOut(left), .rightOut(right),
    .zeroBit(zeroBit));
  fullAdder32bit fulladder32bit_1 (
    .carryIn(1'b0), .A(multiplicand), .B(left), .carryOut(fulladder32bit_1_carryout),
    .sum(fulladder32bit_1_sum));
  Multiplexer #(.enable("false")) multiplexer_1 (
    .in0(1'b0), .in1(fulladder32bit_1_carryout), .out(multiplexer_1_out), .sel(dffS));
  D_Flip_Flop d_ff_1 (.clk(CLK), .D(multiplexer_1_out), .Q(overflow), .en(dffE));  // open: Qn, preset, reset
endmodule

// SF64
module shifter64bit (
  input  [31:0] leftIn,
  input  [31:0] rightIn,
  input  shiftInBit,
  output shiftOutBit,
  output [31:0] rightOut,
  output [31:0] leftOut
);


  assign leftOut = {shiftInBit, leftIn[31:1]};
  assign rightOut = {leftIn[0], rightIn[31:1]};
  assign shiftOutBit = rightIn[0];
endmodule

module shiftRegister64bit (
  input  shiftInBit,
  input  [31:0] leftIn,
  input  [31:0] rightIn,
  input  shiftEn,
  input  leftRest,
  input  CLK,
  input  llE,
  input  lrE,
  output shiftOutBit,
  output zeroBit,
  output [31:0] leftOut,
  output [31:0] rightOut
);

  wire not_1_out;
  wire [31:0] multiplexer_1_out, multiplexer_2_out, multiplexer_3_out, shifter64bit_1_leftout,
       shifter64bit_1_rightout;

  not not_1 (not_1_out, leftRest);
  Multiplexer #(.width(32), .enable("false")) multiplexer_1 (
    .in0(leftIn), .in1(shifter64bit_1_leftout), .out(multiplexer_1_out), .sel(shiftEn));
  Multiplexer #(.width(32), .enable("false")) multiplexer_2 (
    .in0({32{1'b0}}), .in1(multiplexer_1_out), .out(multiplexer_2_out), .sel(not_1_out));
  Register #(.width(32)) leftReg (.D(multiplexer_2_out), .en(llE), .Q(leftOut), .clk(CLK));  // open: clr
  shifter64bit shifter64bit_1 (
    .shiftInBit(shiftInBit), .leftIn(leftOut), .rightIn(rightOut), .leftOut(shifter64bit_1_leftout),
    .rightOut(shifter64bit_1_rightout), .shiftOutBit(shiftOutBit));
  Multiplexer #(.width(32), .enable("false")) multiplexer_3 (
    .in0(rightIn), .in1(shifter64bit_1_rightout), .out(multiplexer_3_out), .sel(shiftEn));
  Register #(.width(32)) rightReg (.D(multiplexer_3_out), .en(lrE), .Q(rightOut), .clk(CLK));  // open: clr

  assign zeroBit = rightOut[0];
endmodule

// FA32
module fullAdder32bit (
  input  [31:0] A,
  input  [31:0] B,
  input  carryIn,
  output carryOut,
  output [31:0] sum
);

  wire fulladder1bit_1_carryout, fulladder1bit_2_carryout, fulladder1bit_3_carryout,
       fulladder1bit_4_carryout, fulladder1bit_5_carryout, fulladder1bit_6_carryout,
       fulladder1bit_7_carryout, fulladder1bit_8_carryout, fulladder1bit_9_carryout,
       fulladder1bit_10_carryout, fulladder1bit_11_carryout, fulladder1bit_12_carryout,
       fulladder1bit_13_carryout, fulladder1bit_14_carryout, fulladder1bit_15_carryout,
       fulladder1bit_16_carryout, fulladder1bit_17_carryout, fulladder1bit_18_carryout,
       fulladder1bit_19_carryout, fulladder1bit_20_carryout, fulladder1bit_21_carryout,
       fulladder1bit_22_carryout, fulladder1bit_23_carryout, fulladder1bit_24_carryout,
       fulladder1bit_25_carryout, fulladder1bit_26_carryout, fulladder1bit_27_carryout,
       fulladder1bit_28_carryout, fulladder1bit_29_carryout, fulladder1bit_30_carryout,
       fulladder1bit_31_carryout;

  fullAdder1bit fulladder1bit_1 (
    .A(A[0]), .B(B[0]), .carryIn(carryIn), .sum(sum[0]), .carryOut(fulladder1bit_1_carryout));
  fullAdder1bit fulladder1bit_2 (
    .A(A[1]), .B(B[1]), .carryIn(fulladder1bit_1_carryout), .sum(sum[1]), .carryOut(fulladder1bit_2_carryout));
  fullAdder1bit fulladder1bit_3 (
    .A(A[2]), .B(B[2]), .carryIn(fulladder1bit_2_carryout), .sum(sum[2]), .carryOut(fulladder1bit_3_carryout));
  fullAdder1bit fulladder1bit_4 (
    .A(A[3]), .B(B[3]), .carryIn(fulladder1bit_3_carryout), .sum(sum[3]), .carryOut(fulladder1bit_4_carryout));
  fullAdder1bit fulladder1bit_5 (
    .A(A[4]), .B(B[4]), .carryIn(fulladder1bit_4_carryout), .sum(sum[4]), .carryOut(fulladder1bit_5_carryout));
  fullAdder1bit fulladder1bit_6 (
    .A(A[5]), .B(B[5]), .carryIn(fulladder1bit_5_carryout), .sum(sum[5]), .carryOut(fulladder1bit_6_carryout));
  fullAdder1bit fulladder1bit_7 (
    .A(A[6]), .B(B[6]), .carryIn(fulladder1bit_6_carryout), .sum(sum[6]), .carryOut(fulladder1bit_7_carryout));
  fullAdder1bit fulladder1bit_8 (
    .A(A[7]), .B(B[7]), .carryIn(fulladder1bit_7_carryout), .sum(sum[7]), .carryOut(fulladder1bit_8_carryout));
  fullAdder1bit fulladder1bit_9 (
    .A(A[8]), .B(B[8]), .carryIn(fulladder1bit_8_carryout), .sum(sum[8]), .carryOut(fulladder1bit_9_carryout));
  fullAdder1bit fulladder1bit_10 (
    .A(A[9]), .B(B[9]), .carryIn(fulladder1bit_9_carryout), .sum(sum[9]), .carryOut(fulladder1bit_10_carryout));
  fullAdder1bit fulladder1bit_11 (
    .A(A[10]), .B(B[10]), .carryIn(fulladder1bit_10_carryout), .sum(sum[10]),
    .carryOut(fulladder1bit_11_carryout));
  fullAdder1bit fulladder1bit_12 (
    .A(A[11]), .B(B[11]), .carryIn(fulladder1bit_11_carryout), .sum(sum[11]),
    .carryOut(fulladder1bit_12_carryout));
  fullAdder1bit fulladder1bit_13 (
    .A(A[12]), .B(B[12]), .carryIn(fulladder1bit_12_carryout), .sum(sum[12]),
    .carryOut(fulladder1bit_13_carryout));
  fullAdder1bit fulladder1bit_14 (
    .A(A[13]), .B(B[13]), .carryIn(fulladder1bit_13_carryout), .sum(sum[13]),
    .carryOut(fulladder1bit_14_carryout));
  fullAdder1bit fulladder1bit_15 (
    .A(A[14]), .B(B[14]), .carryIn(fulladder1bit_14_carryout), .sum(sum[14]),
    .carryOut(fulladder1bit_15_carryout));
  fullAdder1bit fulladder1bit_16 (
    .A(A[15]), .B(B[15]), .carryIn(fulladder1bit_15_carryout), .sum(sum[15]),
    .carryOut(fulladder1bit_16_carryout));
  fullAdder1bit fulladder1bit_17 (
    .A(A[16]), .B(B[16]), .carryIn(fulladder1bit_16_carryout), .sum(sum[16]),
    .carryOut(fulladder1bit_17_carryout));
  fullAdder1bit fulladder1bit_18 (
    .A(A[17]), .B(B[17]), .carryIn(fulladder1bit_17_carryout), .sum(sum[17]),
    .carryOut(fulladder1bit_18_carryout));
  fullAdder1bit fulladder1bit_19 (
    .A(A[18]), .B(B[18]), .carryIn(fulladder1bit_18_carryout), .sum(sum[18]),
    .carryOut(fulladder1bit_19_carryout));
  fullAdder1bit fulladder1bit_20 (
    .A(A[19]), .B(B[19]), .carryIn(fulladder1bit_19_carryout), .sum(sum[19]),
    .carryOut(fulladder1bit_20_carryout));
  fullAdder1bit fulladder1bit_21 (
    .A(A[20]), .B(B[20]), .carryIn(fulladder1bit_20_carryout), .sum(sum[20]),
    .carryOut(fulladder1bit_21_carryout));
  fullAdder1bit fulladder1bit_22 (
    .A(A[21]), .B(B[21]), .carryIn(fulladder1bit_21_carryout), .sum(sum[21]),
    .carryOut(fulladder1bit_22_carryout));
  fullAdder1bit fulladder1bit_23 (
    .A(A[22]), .B(B[22]), .carryIn(fulladder1bit_22_carryout), .sum(sum[22]),
    .carryOut(fulladder1bit_23_carryout));
  fullAdder1bit fulladder1bit_24 (
    .A(A[23]), .B(B[23]), .carryIn(fulladder1bit_23_carryout), .sum(sum[23]),
    .carryOut(fulladder1bit_24_carryout));
  fullAdder1bit fulladder1bit_25 (
    .A(A[24]), .B(B[24]), .carryIn(fulladder1bit_24_carryout), .sum(sum[24]),
    .carryOut(fulladder1bit_25_carryout));
  fullAdder1bit fulladder1bit_26 (
    .A(A[25]), .B(B[25]), .carryIn(fulladder1bit_25_carryout), .sum(sum[25]),
    .carryOut(fulladder1bit_26_carryout));
  fullAdder1bit fulladder1bit_27 (
    .A(A[26]), .B(B[26]), .carryIn(fulladder1bit_26_carryout), .sum(sum[26]),
    .carryOut(fulladder1bit_27_carryout));
  fullAdder1bit fulladder1bit_28 (
    .A(A[27]), .B(B[27]), .carryIn(fulladder1bit_27_carryout), .sum(sum[27]),
    .carryOut(fulladder1bit_28_carryout));
  fullAdder1bit fulladder1bit_29 (
    .A(A[28]), .B(B[28]), .carryIn(fulladder1bit_28_carryout), .sum(sum[28]),
    .carryOut(fulladder1bit_29_carryout));
  fullAdder1bit fulladder1bit_30 (
    .A(A[29]), .B(B[29]), .carryIn(fulladder1bit_29_carryout), .sum(sum[29]),
    .carryOut(fulladder1bit_30_carryout));
  fullAdder1bit fulladder1bit_31 (
    .A(A[30]), .B(B[30]), .carryIn(fulladder1bit_30_carryout), .sum(sum[30]),
    .carryOut(fulladder1bit_31_carryout));
  fullAdder1bit fulladder1bit_32 (
    .A(A[31]), .B(B[31]), .carryIn(fulladder1bit_31_carryout), .sum(sum[31]), .carryOut(carryOut));
endmodule

// FA
module fullAdder1bit (
  input  A,
  input  B,
  input  carryIn,
  output sum,
  output carryOut
);

  wire and_1_out, and_2_out, xor_1_out;

  xor xor_1 (xor_1_out, A, B);
  and and_1 (and_1_out, A, B);
  xor xor_2 (sum, xor_1_out, carryIn);
  and and_2 (and_2_out, carryIn, xor_1_out);
  or or_1 (carryOut, and_2_out, and_1_out);
endmodule
