// Logisim project mult32.circ as structural Verilog: 7 circuits, main circuit main
module main (
  output [31:0] product_left,
  output [31:0] product_right
);

  wire clock_1_out, main_1_ce, main_1_clr, main_1_diffe, main_1_diffs, main_1_lle, main_1_lre, main_2_cout,
       main_2_zerobit, Start_out;
  wire [31:0] test_2_1_multiplicand, test_2_1_multiplier;

  test_1 test_1_1 ();  // open: CLK, Multiplicand, Multiplier
  Button Start (.out(Start_out));
  Clock clock_1 (.out(clock_1_out));
  test_3 test_3_1 ();  // open: CLK, Multiplicand, Multiplier
  test_2 test_2_1 (.CLK(clock_1_out), .Multiplicand(test_2_1_multiplicand), .Multiplier(test_2_1_multiplier));
  control_main main_1 (
    .zb(main_2_zerobit), .button(Start_out), .cout(main_2_cout), .CLK(clock_1_out), .diffE(main_1_diffe),
    .llE(main_1_lle), .lrE(main_1_lre), .clr(main_1_clr), .CE(main_1_ce), .diffS(main_1_diffs));
  test_4 test_4_1 ();  // open: CLK, Multiplicand, Multiplier
  datapath_main main_2 (
    .CE(main_1_ce), .clr(main_1_clr), .llE(main_1_lle), .lrE(main_1_lre),
    .multiplicand(test_2_1_multiplicand), .dffS(main_1_diffs), .CLK(clock_1_out), .dffE(main_1_diffe),
    .cout(main_2_cout), .multiplier(test_2_1_multiplier), .zeroBit(main_2_zerobit), .right(product_right),
    .left(product_left));  // open: shfOut, overflow
  test_5 test_5_1 ();  // open: CLK, Multiplicand, Multiplier
  test_6 test_6_1 ();  // open: CLK, Multiplicand, Multiplier

  // Notes on the sheet:
  //   You can calculate calculate pressing by start button
  //   Test cases can be checked out on their own circuit
  //   Test can be wired to main circuit
endmodule

// 1
module test_1 (
  input  CLK,
  output [31:0] Multiplicand,
  output [31:0] Multiplier
);

  Register #(.width(32)) register_1 (.D(32'h2), .en(1'b1), .Q(Multiplicand), .clk(CLK));  // open: clr
  Register #(.width(32)) register_2 (.D(32'h6), .en(1'b1), .Q(Multiplier), .clk(CLK));  // open: clr

  // Notes on the sheet:
  //   Integer 2
  //   Integer 6
  //   Expected result: 12
endmodule

// 2
module test_2 (
  input  CLK,
  output [31:0] Multiplicand,
  output [31:0] Multiplier
);

  Register #(.width(32)) register_1 (.D(32'h36), .en(1'b1), .Q(Multiplicand), .clk(CLK));  // open: clr
  Register #(.width(32)) register_2 (.D(32'h19), .en(1'b1), .Q(Multiplier), .clk(CLK));  // open: clr

  // Notes on the sheet:
  //   Integer 54
  //   Integer 25
  //   Expected result: 1350
endmodule

// 3
module test_3 (
  input  CLK,
  output [31:0] Multiplicand,
  output [31:0] Multiplier
);

  Register #(.width(32)) register_1 (.D(32'hfe), .en(1'b1), .Q(Multiplicand), .clk(CLK));  // open: clr
  Register #(.width(32)) register_2 (.D(32'h71), .en(1'b1), .Q(Multiplier), .clk(CLK));  // open: clr

  // Notes on the sheet:
  //   Integer 254
  //   Integer 113
  //   Expected result: 28.702
endmodule

// 4
module test_4 (
  input  CLK,
  output [31:0] Multiplicand,
  output [31:0] Multiplier
);

  Register #(.width(32)) register_1 (.D(32'h459), .en(1'b1), .Q(Multiplicand), .clk(CLK));  // open: clr
  Register #(.width(32)) register_2 (.D(32'hbc6), .en(1'b1), .Q(Multiplier), .clk(CLK));  // open: clr

  // Notes on the sheet:
  //   Integer 1113
  //   Integer 3014
  //   Expected result: 3.354.582
endmodule

// 5
module test_5 (
  input  CLK,
  output [31:0] Multiplicand,
  output [31:0] Multiplier
);

  Register #(.width(32)) register_1 (.D(32'had44), .en(1'b1), .Q(Multiplicand), .clk(CLK));  // open: clr
  Register #(.width(32)) register_2 (.D(32'hdbfa), .en(1'b1), .Q(Multiplier), .clk(CLK));  // open: clr

  // Notes on the sheet:
  //   Integer 44356
  //   Integer 56314
  //   Expected result: 2.497.863.784
endmodule

// 6
module test_6 (
  input  CLK,
  output [31:0] Multiplicand,
  output [31:0] Multiplier
);

  Register #(.width(32)) register_1 (.D({32{1'b1}}), .en(1'b1), .Q(Multiplicand), .clk(CLK));  // open: clr
  Register #(.width(32)) register_2 (.D(32'hd), .en(1'b1), .Q(Multiplier), .clk(CLK));  // open: clr

  // Notes on the sheet:
  //   Integer 4294967295
  //   Integer 13
  //   Expected result: 55.834.574.835
endmodule
